# Fritzing sketch Door_status (saved by Fritzing 0.9.3b)
breadboards: 1

parts:
  元件1 = Arduino Mega 2560 (Rev3)
  R1 = Rotary Potentiometer (Small) [maximum_resistance=100kΩ package=THT]
  LCD1 = LCD screen
  R2 = Resistor [tolerance=±5% resistance=330 package=THT]
  hc-sr1 = hc-sr04

nets:
  N1: 元件1.D12_PWM, LCD1.E
  N2: 元件1.D11_PWM, LCD1.RS
  N3: 元件1.D10_PWM, hc-sr1.Trig
  N4: 元件1.D9_PWM, hc-sr1.Echo
  5V: 元件1.5V, R1.leg2, LCD1.VDD, R2.Pin_1, hc-sr1.VCC
  GND: 元件1.GND, R1.leg1, LCD1.VSS, LCD1.R/W, LCD1.LED-, hc-sr1.GND
  N5: 元件1.D3_PWM, LCD1.DB7
  N6: 元件1.D4_PWM, LCD1.DB6
  N7: 元件1.D5_PWM, LCD1.DB5
  N8: 元件1.D6_PWM, LCD1.DB4
  N9: R1.wiper, LCD1.V0
  N10: LCD1.LED+, R2.Pin_0
